# Fritzing sketch Line follower wiring schematic (saved by Fritzing 0.9.6b)
breadboards: 1

parts:
  M1 = gear-motor [part_number="MOTOR LEFT"]
  M2 = gear-motor [part_number="MOTOR RIGHT"]
  Part1 = Arduino Uno (Rev3)
  BAT1 = BC9VPC [package=bc9vpc]
  VCC1 = 4 x AAA Battery Mount
  M3 = 5-ir-array-sensor [package=THT]
  HC-SR04_Sensor_1 = HC-SR04 Ultrasonic Distance Sensor
  U1 = L9110 H-bridge module [part_number="L9110 H-bridge"]

nets:
  N1: M1.pin_1, U1.MOTOR_B-B
  N2: M1.pin_2, U1.MOTOR_B-A
  N3: M2.pin_1, U1.MOTOR_A-A
  N4: M2.pin_2, U1.MOTOR_A-B
  N5: Part1.A0, M3.S1
  N6: Part1.A1, M3.S2
  N7: Part1.A2, M3.S3
  N8: Part1.A3, M3.S4
  N9: Part1.A4/SDA, M3.S5
  N10: Part1.D2, U1.A-IB
  N11: Part1.D3_PWM, U1.A-IA
  N12: Part1.D4, U1.B-IB
  N13: Part1.D5_PWM, U1.B-IA
  3V3: Part1.3V3, M3.VCC
  5V: Part1.5V, HC-SR04_Sensor_1.VCC
  GND: Part1.GND, BAT1.V-, HC-SR04_Sensor_1.GND
  N14: Part1.VIN, BAT1.V+
  N15: VCC1.-, U1.VCC

custom parts:
  5-ir-array-sensor: 5 IR array sensor.
